# Fritzing sketch sketch (saved by Fritzing 0.9.3b)
breadboards: 2

parts:
  S1 = H-Bridge with L298N
  BT1 = Bluetooth HC-06u [package=THT]
  부품1 = Arduino Uno (Rev3)
  VCC1 = Battery block 9V
  M1 = DC Motor
  M2 = DC Motor

nets:
  N1: S1.12V, VCC1.+
  GND: S1.GND, BT1.GND, 부품1.GND, VCC1.-
  N2: S1.IN1, 부품1.D6_PWM
  N3: S1.IN2, 부품1.D7
  N4: S1.IN3, 부품1.D11_PWM/MOSI
  N5: S1.IN4, 부품1.D12/MISO
  N6: S1.M1-01, M1.pin_1
  N7: S1.M1-02, M1.pin_2
  N8: S1.M2-01, M2.pin_2
  N9: S1.M2-02, M2.pin_1
  VCC: BT1.VCC, 부품1.5V
  N10: BT1.TXD, 부품1.D2
  N11: BT1.RXD, 부품1.D3_PWM

custom parts:
  H-Bridge with L298N: h-bridge
  Bluetooth HC-06u: Bluetooth HC-06 - face up, pins down 16.5mm x 37.5mm PCB
